// Logisim project adder.circ as structural Verilog: 4 circuits, main circuit byte_adder
module half_adder (
  input  A,
  input  B,
  output S,
  output Cout
);

  and and_1 (Cout, B, A);
  xor xor_1 (S, A, B);
endmodule

module full_adder (
  input  A,
  input  B,
  input  Cin,
  output S,
  output Cout
);

  wire and_1_out, and_2_out, xor_1_out;

  xor xor_1 (xor_1_out, A, B);
  and and_1 (and_1_out, A, B);
  xor xor_2 (S, xor_1_out, Cin);
  and and_2 (and_2_out, xor_1_out, Cin);
  or or_1 (Cout, and_2_out, and_1_out);
endmodule

module four_bit_adder (
  input  in_1,
  input  in_2,
  input  B0,
  input  A0,
  input  D1,
  input  C1,
  input  B1,
  input  A1,
  input  in_9,
  output Cout,
  output S3,
  output S2,
  output S1,
  output S0
);

  wire full_adder_2_cout, full_adder_3_cout, full_adder_4_cout;

  full_adder full_adder_1 (.A(in_1), .B(D1), .Cin(full_adder_2_cout), .S(S3), .Cout(Cout));
  full_adder full_adder_2 (.A(in_2), .B(C1), .Cin(full_adder_3_cout), .S(S2), .Cout(full_adder_2_cout));
  full_adder full_adder_3 (.A(B0), .B(B1), .Cin(full_adder_4_cout), .S(S1), .Cout(full_adder_3_cout));
  full_adder full_adder_4 (.A(A0), .B(A1), .Cin(in_9), .S(S0), .Cout(full_adder_4_cout));
endmodule

module byte_adder (
  input  A,
  input  _6,
  input  _5,
  input  _4,
  input  _3,
  input  _2,
  input  _1,
  input  _0,
  input  B,
  input  in_10,
  input  in_11,
  input  in_12,
  input  in_13,
  input  in_14,
  input  in_15,
  input  in_16,
  input  in_17,
  output out_18,
  output out_19,
  output out_20,
  output out_21,
  output out_22,
  output out_23,
  output out_24,
  output out_25,
  output out_26
);

  wire four_bit_adder_2_cout;

  four_bit_adder four_bit_adder_1 (
    .in_1(A), .D1(B), .in_2(_6), .C1(in_10), .B0(_5), .B1(in_11), .A0(_4), .A1(in_12),
    .in_9(four_bit_adder_2_cout), .S3(out_19), .S2(out_20), .S1(out_21), .S0(out_22), .Cout(out_18));
  four_bit_adder four_bit_adder_2 (
    .in_1(_3), .D1(in_13), .in_2(_2), .C1(in_14), .B0(_1), .B1(in_15), .A0(_0), .A1(in_16), .in_9(in_17),
    .S3(out_23), .S2(out_24), .S1(out_25), .S0(out_26), .Cout(four_bit_adder_2_cout));

  // Notes on the sheet:
  //   7
endmodule
